# Fritzing sketch Schema (saved by Fritzing 0.9.2b)

parts:
  Onderdeel1 = Arduino Uno (Rev3)
  T1 = TMP36 Temperature Sensor [package="TO92 [THT]"]
  R1 = Rotary Potentiometer (Small) [maximum_resistance=100kΩ package=THT]
  LCD1 = LCD screen
  R2 = TRIMPOT [package=trimpot-5mm]

nets:
  N1: Onderdeel1.A4/SDA, R1.wiper
  N2: Onderdeel1.A5/SCL, T1.+Vs
  GND: Onderdeel1.GND, R1.leg1, LCD1.VSS
  N3: Onderdeel1.D2, LCD1.DB7
  N4: Onderdeel1.D3_PWM, LCD1.DB6
  N5: Onderdeel1.D4, LCD1.DB5
  N6: Onderdeel1.D5_PWM, LCD1.DB4
  N7: Onderdeel1.D6_PWM, LCD1.RS
  N8: Onderdeel1.D7, LCD1.E
  N9: Onderdeel1.5V, R1.leg2
  N10: LCD1.V0, R2.CW
